# Fritzing sketch final (saved by Fritzing 0.9.1b)

parts:
  부품1 = Arduino Micro (Rev3)
  J1 = Infrared Proximity Sensor
  J2 = Infrared Proximity Sensor
  J3 = Infrared Proximity Sensor
  U1 = Vibration Motor- ROB-08449 [package=vibe-motor-10mm]
  U2 = Vibration Motor- ROB-08449 [package=vibe-motor-10mm]
  U3 = Vibration Motor- ROB-08449 [package=vibe-motor-10mm]
  U4 = CAPSENSE_PAD [package=capsense_pad]
  U5 = LIPO-2000mAh [package=lipo-2000]
  부품2 = USB LiPoly Charger
  D1 = SOLAR-IXYS [package=solarbit-12x1]  # not connected

nets:
  GND: 부품1.GND, J1.GND, J2.GND, J3.GND, U1.+, U2.+, U3.+, U4.RES, U5.-, 부품2.GND
  N1: 부품1.D2/SDA, J2.Vout
  N2: 부품1.D3/SCL, U3.-
  N3: 부품1.D4_PWM/A6, J1.Vout
  N4: 부품1.D5_PWM, U1.-
  N5: 부품1.D6_PWM/A7, J3.Vout
  N6: 부품1.D7, U2.-
  N7: 부품1.VIN, U5.+, 부품2.VBAT
  VCC: 부품1.5V, J1.Vcc, J2.Vcc, J3.Vcc
  N8: 부품1.A0, U4.RECEIVE
