# Fritzing sketch PLD (saved by Fritzing 0.9.1b)
breadboards: 1

parts:
  Part1 = Arduino Uno (Rev3)
  Power_plug1 = Power plug
  R1 = Resistor [tolerance=±5% resistance=1k package=THT]
  Q1 = npn-Powertransistor [part_number=TIP102 package="TO220 [THT]"]
  D2 = Rectifier Diode [part_number=1N4004 package="300 mil [THT]"]  # not connected
  L1 = Solenoid
  Part2 = Bluetooth Mate Silver
  J1 = Piezo Speaker
  S2 = Reed switch [package=THT]

nets:
  N1: Part1.D8, R1.Pin_0
  N2: Part1.D10_PWM/SS, J1.pin2
  GND: Part1.GND, Power_plug1.GND, Q1.emitter, Part2.GND, J1.pin1, S2.pin_1
  N3: Part1.D0/RX, Part2.TX_5V
  N4: Part1.D1/TX, Part2.RX_5V
  N5: Part1.D7, S2.pin_2
  3V3: Part1.3V3, Part2.VCC
  N6: Power_plug1.VCC, L1.pin2
  N7: R1.Pin_1, Q1.base
  N8: Q1.collector, L1.pin1
