# Fritzing sketch ITM492 (saved by Fritzing 0.9.2b)

parts:
  Part1 = Arduino Board Ethernet
  IC1 = IC, DIP package, 8 pins [chip_label="HID RFID"]

nets:
  N1: Part1.D2_PWM, IC1.pin1
  N2: Part1.D3_PWM, IC1.pin2
  N3: Part1.5V, IC1.pin8
  N4: Part1.GND, IC1.pin7
