# Fritzing sketch Security System Circuit (saved by Fritzing 0.9.1b)
breadboards: 1

parts:
  Part1 = IOIO for Android
  U3 = RELAY [package=relay-jzc]
  SPKR1 = Loudspeaker
  VCC1 = Battery block 9V  # not connected

nets:
  N1: Part1.PIN1, U3.NC
  N2: Part1.5V, U3.NO
  N3: Part1.GND, U3.COIL2
  N4: U3.COIL1, SPKR1.pin2
