# Fritzing sketch BJVteam__Access_and_Attendance_Final (saved by Fritzing 0.9.2b)
breadboards: 2

parts:
  Part1 = Arduino Uno (Rev3)
  Part2 = Real Time Clock Module - DS1307 RTC Breakout Board
  Part4 = Arduino Uno (Rev3)
  Part5 = Real Time Clock Module - DS1307 RTC Breakout Board
  Part6 = Arduino Ethernet Shield (Rev3)  # not connected
  Part7 = Arduino Ethernet Shield (Rev3)  # not connected
  Part8 = Arduino Mega 2560 (Rev3)  # not connected

nets:
  N1: Part1.A4/SDA, Part2.SDA
  N2: Part1.A5/SCL, Part2.SCL
  N3: Part1.5V, Part2.SQW
  GND: Part1.GND, Part2.GND
  N4: Part4.A4/SDA, Part5.SDA
  N5: Part4.A5/SCL, Part5.SCL
  N6: Part4.5V, Part5.SQW
  GND_2: Part4.GND, Part5.GND

notes:
  RFID Reader
  (HID Prox Pro II)
  RELAY Board
  BATTERY
  Door opener
  RFID Reader
