# Fritzing sketch Chromiris (saved by Fritzing 0.9.2b)
breadboards: 2

parts:
  Part1 = Arduino Uno (Rev3)
  U1 = LCD-16X2 [package=lcd-16x2_noholes]
  S1 = Momentary Switch [package=ksa_sealed_tac_switch]
  SENSOR1 = TCS34725 RGB Color Sensor
  R1 = Resistor [tolerance=±5% resistance=220 package="1206 [SMD]"]
  R3 = Resistor [tolerance=±5% resistance=1k package="0603 [SMD]"]

nets:
  N1: Part1.A4/SDA, SENSOR1.SDA
  N2: Part1.A5/SCL, SENSOR1.SCL
  N3: Part1.D11_PWM/MOSI, U1.E
  N4: Part1.D12/MISO, U1.RS
  N5: Part1.D2, U1.DB7
  N6: Part1.D3_PWM, U1.DB6
  N7: Part1.D4, U1.DB5
  N8: Part1.D5_PWM, U1.DB4
  N9: Part1.D7, S1.1, R3.Pin_1
  VDD: Part1.5V, U1.VDD, S1.3, SENSOR1.VDD, R1.Pin_1
  GND: Part1.GND, U1.VSS, U1.VO, U1.R_W, U1.K, SENSOR1.GND, R3.Pin_0
  N10: U1.A, R1.Pin_0

custom parts:
  TCS34725 RGB Color Sensor: TCS34725 RGB Color Sensor with LED
