# Fritzing sketch Sensor 4 (saved by Fritzing 0.9.2b)
breadboards: 1

parts:
  U2 = XBEE-1 [package=xbee-1]
  VCC1 = Battery

nets:
  N1: U2.VDD, VCC1.+
  N2: U2.GND, VCC1.-

notes:
  MQ2 Sensor 2
  Pinout
  G V S
