# Fritzing sketch Final Project (saved by Fritzing 0.9.1b)
breadboards: 2

parts:
  Arduino_Sound_Detector_and_Interrupt_Generator_(Analog_INPUT_-_Digital_OUTPUT) = Arduino Uno (Rev3)
  Time_Interrupt_Analyzer_and_Position_Control_(Interrupt_Ports) = Arduino Mega 2560 (Rev3)
  Front_Microphone = Breakout Board for Electret Microphone
  Left_Microphone = Breakout Board for Electret Microphone
  Back_Microphone = Breakout Board for Electret Microphone
  Right_Microphone = Breakout Board for Electret Microphone
  LED1 = LED - 5mm [color="Red (633nm)" package="5 mm [THT]"]
  LED2 = LED - 5mm [color="Red (633nm)" package="5 mm [THT]"]
  LED3 = LED - 5mm [color="Green (570nm)" package="5 mm [THT]"]
  LED4 = LED - 5mm [color="Green (570nm)" package="5 mm [THT]"]

nets:
  N1: Arduino_Sound_Detector_and_Interrupt_Generator_(Analog_INPUT_-_Digital_OUTPUT).A0, Right_Microphone.AUD
  N2: Arduino_Sound_Detector_and_Interrupt_Generator_(Analog_INPUT_-_Digital_OUTPUT).A1, Back_Microphone.AUD
  N3: Arduino_Sound_Detector_and_Interrupt_Generator_(Analog_INPUT_-_Digital_OUTPUT).A2, Left_Microphone.AUD
  N4: Arduino_Sound_Detector_and_Interrupt_Generator_(Analog_INPUT_-_Digital_OUTPUT).A3, Front_Microphone.AUD
  N5: Arduino_Sound_Detector_and_Interrupt_Generator_(Analog_INPUT_-_Digital_OUTPUT).D4, Time_Interrupt_Analyzer_and_Position_Control_(Interrupt_Ports).D18/TX1
  N6: Arduino_Sound_Detector_and_Interrupt_Generator_(Analog_INPUT_-_Digital_OUTPUT).D5_PWM, Time_Interrupt_Analyzer_and_Position_Control_(Interrupt_Ports).D19/RX1
  N7: Arduino_Sound_Detector_and_Interrupt_Generator_(Analog_INPUT_-_Digital_OUTPUT).D6_PWM, Time_Interrupt_Analyzer_and_Position_Control_(Interrupt_Ports).D20/SDA
  N8: Arduino_Sound_Detector_and_Interrupt_Generator_(Analog_INPUT_-_Digital_OUTPUT).D7, Time_Interrupt_Analyzer_and_Position_Control_(Interrupt_Ports).D21/SCL
  VCC: Arduino_Sound_Detector_and_Interrupt_Generator_(Analog_INPUT_-_Digital_OUTPUT).5V, Front_Microphone.VCC, Left_Microphone.VCC, Back_Microphone.VCC, Right_Microphone.VCC
  GND: Arduino_Sound_Detector_and_Interrupt_Generator_(Analog_INPUT_-_Digital_OUTPUT).GND, Time_Interrupt_Analyzer_and_Position_Control_(Interrupt_Ports).GND, Front_Microphone.GND, Left_Microphone.GND, Back_Microphone.GND, Right_Microphone.GND, LED1.cathode, LED2.cathode, LED3.cathode, LED4.cathode
  N9: Time_Interrupt_Analyzer_and_Position_Control_(Interrupt_Ports).D13_PWM, LED3.anode
  N10: Time_Interrupt_Analyzer_and_Position_Control_(Interrupt_Ports).D12_PWM, LED4.anode
  N11: Time_Interrupt_Analyzer_and_Position_Control_(Interrupt_Ports).D11_PWM, LED2.anode
  N12: Time_Interrupt_Analyzer_and_Position_Control_(Interrupt_Ports).D10_PWM, LED1.anode
